# Fritzing sketch FruitMachineButtons (saved by Fritzing 0.9.3b)

parts:
  BUTTON1 = Arcade Button (white)
  LED1 = RGB LED (com. cathode, rgb) [package="5 mm [THT]"]
  Part1 = Arduino Nano (Rev3.0) (ICSP)
  LED2 = RGB LED (com. cathode, rgb) [package="5 mm [THT]"]
  LED3 = RGB LED (com. cathode, rgb) [package="5 mm [THT]"]
  LED4 = RGB LED (com. cathode, rgb) [package="5 mm [THT]"]

nets:
  N1: BUTTON1.no_name_yet#1, Part1.D2
  N2: BUTTON1.no_name_yet#2, LED1.common_cathode, Part1.GND, LED2.common_cathode, LED3.common_cathode, LED4.common_cathode
  N3: LED1.red_anode, LED2.blue_anode
  N4: LED1.green_anode, Part1.5V, LED2.green_anode, LED3.green_anode, LED4.green_anode
  N5: LED1.blue_anode, Part1.A0
  N6: LED2.red_anode, LED3.blue_anode
  N7: LED3.red_anode, LED4.blue_anode

notes:
  Additional PL9823 may be connected in series, with Data Out of each LED connected to Data In of the next. Note that, unlike WS2812B/Neopixels, PL9823 do not require a series resistor on the data line to the Arduino.
  To identify legs of the PL9823, note the flat side of the LED (shown here on the left), starting from which:
  - Data Out
  - Ground
  - VCC (4.5V - 6V)
  - Data In

custom parts:
  Arcade Button (white): Adafruit Arcade Button (white)
