# Fritzing sketch FruitMachineCounter (saved by Fritzing 0.9.3b)

parts:
  J1 = female pin header, 2 pins [form="♀ (female)"]  # not connected
  Part1 = Arduino Nano (Rev3.0)
  SEC = female pin header, 6 pins [form="♀ (female)"]
  SEC_2 = female pin header, 6 pins [form="♀ (female)"]

nets:
  GND: Part1.GND, SEC.pin6, SEC_2.pin6
  N1: Part1.D11/MOSI, SEC.pin3, SEC_2.pin3
  N2: Part1.D12/MISO, SEC.pin1, SEC_2.pin1
  N3: Part1.D13/SCK, SEC.pin2, SEC_2.pin2
  12V: SEC.pin5, SEC_2.pin5

notes:
  Every time a 12V pulse is received (i.e. 12V is supplied and disconnected), counter increases by one.
  Polarity of the wires doesn't seem to matter, and connecting them the other way around works exactly the same (there is no way to make the counter decrease, or zero it)
  12V DC
  The Electronic Starpoint meter replaces all mechanical meters and provides the meter information as follow in 10p units:
  Meter
  REFILL
  CASH IN
  CASH OUT
  CHANGE
  PRIZES OUT
  VTP
  NOTES IN
  In normal operation the electronic meter will display meter 1 which is the refill meter.
  According to
  https://www.mikrocontroller.net/attachment/163201/Zaehlwerk_27-080_01__man.pdf
  Interface is:
  Pin Signal Name Type Description
  1 SOUT Output SPI Data Output Line
  2 SCLOCK Input SPI Clock Input Line
  3 SIN Input SPI Data Input Line
  4 Reset Input SEC Reset (Low)
  5 +12v Input DC Voltage Supply
  6 GND Input 0v Supply
  Mechanical Counters
  Electronic Counters
  1. SOUT
  2. SCLOCK
  3. SIN
  4. Reset (NC)
  5. +12v
  6. GND
