# Fritzing sketch FruitMachineHopper (saved by Fritzing 0.9.3b)

parts:
  Part1 = Arduino Nano (Rev3.0)
  D2 = Rectifier Diode [part_number=1N4001 package="300 mil [THT]"]
  R3 = Resistor [tolerance=±5% resistance=10k package=THT]
  J1 = female pin header, 10 pins [form="♀ (female)"]
  JACK1 = 2.1mm Barrel Jack with Terminal Block
  Part2 = Arduino Nano (Rev3.0)
  JACK2 = 2.1mm Barrel Jack with Terminal Block
  J2 = female pin header, 4 pins [form="♀ (female)"]
  KY-1 = Keyes Relay [package=THT]

nets:
  N1: Part1.GND, J1.pin7
  N2: Part1.D8, D2.anode, R3.Pin_0, J1.pin8
  N3: Part1.D9, D2.cathode
  N4: Part1.5V, R3.Pin_1
  N5: J1.pin4, JACK1.POS
  N6: J1.pin6, JACK1.NEG
  N7: Part2.D2, KY-1.signal
  N8: Part2.D4, J2.pin4
  N9: Part2.GND, KY-1.ground
  N10: Part2.5V, KY-1.power
  N11: JACK2.POS, J2.pin1
  N12: JACK2.NEG, KY-1.NO
  N13: J2.pin2, KY-1.C

notes:
  CCTalk uses a single bi-directional data line, but Arduino uses separate Rx/Tx lines, so we need to combine them. For this we use a diode, and an external pullup as shown
  (This is assuming using AltSoftSerial, where Tx=9, Rx=8)
  For more info:
  https://cctalktutorial.wordpress.com/2016/07/28/cctalk-tutorial-cctalk-on-arduino-nano-part-1/
  https://cctalktutorial.wordpress.com/2015/08/11/cctalk-tutorial-the-hardware-interface/
  https://forum.arduino.cc/t/cctalk-on-mega-2560/579887/8
  CCTALK serial interface
  1 Address Sel 3 - MSB
  2 Address Sel 2
  3 Address Sel 1 - LSB
  4 +24V
  5 +24V
  6 0V
  7 0V
  8 DATA
  9 N/C
  10 RESET
  In this example, no Address lines are attached, so address = 3. If Pin 3 were attached, address = 4, etc, up to 10.
  The parallel interface is simple: the hopper will dispense coins for as long as the power supply is connected. Every time a coin is dispensed, the coin count pin switches from open collector output to 0V, so if connected to a GPIO pin with INPUT_PULLUP enabled, will register as a LOW pulse.
  Once a sufficient number of pulses have been detected, the Arduino can disconnect the power
  Parallel interface
  1 +24 V
  2 GND
  3 Opto Supply
  4 Coin Count Output

custom parts:
  Keyes Relay: The Keyes 5V relay module is suitable for SCM development, home appliance control. It uses a 5V~12V TIL control signal which can control DC / AC signal.
