# Fritzing sketch FruitMachineLED (saved by Fritzing 0.9.3b)
circuit board: 10cm x 6cm
breadboards: 2

parts:
  Arduino = Arduino Nano (Rev3.0)
  8-Channel_Source = DIP - 18 pins [package="DIP (Dual Inline) [THT]"]
  Shift_Register = 74HC595 [package="DIP16 [THT]"]
  C1 = Ceramic Capacitor [capacitance=100nF package="100 mil [THT, multilayer]"]
  R1 = Resistor [tolerance=±5% resistance=330 package=THT]
  R3 = Resistor [tolerance=±5% resistance=330 package=THT]
  R4 = Resistor [tolerance=±5% resistance=330 package=THT]
  R5 = Resistor [tolerance=±5% resistance=330 package=THT]
  R6 = Resistor [tolerance=±5% resistance=330 package=THT]
  R7 = Resistor [tolerance=±5% resistance=330 package=THT]
  R8 = Resistor [tolerance=±5% resistance=470 package=THT]
  DI2 = 7 Segment Display
  8-Channel_Sink = ULN2803A [package=THT]
  DI3 = 7 Segment Display
  DI4 = 7 Segment Display
  DI5 = 7 Segment Display
  DI6 = 7 Segment Display
  R9 = Resistor [tolerance=±5% resistance=330 package=THT]
  Shift_Register_2 = 74HC595 [package="DIP16 [THT]"]
  C2 = Ceramic Capacitor [capacitance=100nF package="100 mil [THT, multilayer]"]
  C3 = Ceramic Capacitor [capacitance=100nF package="100 mil [THT, multilayer]"]
  Arduino1 = Arduino Nano (Rev3.0)
  C4 = Ceramic Capacitor [capacitance=100nF package="100 mil [THT, multilayer]"]
  IC4 = IC, DIP package, 16 pins [chip_label=MIC5891]
  R14 = Resistor [tolerance=±5% resistance=330 package=THT]
  R10 = Resistor [tolerance=±5% resistance=470 package=THT]
  R15 = Resistor [tolerance=±5% resistance=330 package=THT]
  R12 = Resistor [tolerance=±5% resistance=330 package=THT]
  R11 = Resistor [tolerance=±5% resistance=330 package=THT]
  R17 = Resistor [tolerance=±5% resistance=330 package=THT]
  R13 = Resistor [tolerance=±5% resistance=330 package=THT]
  R16 = Resistor [tolerance=±5% resistance=330 package=THT]
  DI11 = 7 Segment Display
  DI10 = 7 Segment Display
  DI9 = 7 Segment Display
  DI8 = 7 Segment Display
  IC5 = IC, DIP package, 20 pins [chip_label=TPIC6B595]
  DI12 = 7 Segment Display
  R18 = Resistor [tolerance=±5% resistance=4.7k package=THT]
  R19 = Resistor [tolerance=±5% resistance=4.7k package=THT]
  R20 = Resistor [tolerance=±5% resistance=4.7k package=THT]
  R21 = Resistor [tolerance=±5% resistance=4.7k package=THT]
  R22 = Resistor [tolerance=±5% resistance=4.7k package=THT]
  R23 = Resistor [tolerance=±5% resistance=4.7k package=THT]
  R24 = Resistor [tolerance=±5% resistance=4.7k package=THT]
  R25 = Resistor [tolerance=±5% resistance=4.7k package=THT]
  Part1 = Arduino Nano (Rev3.0)
  IC1 = IC, DIP package, 16 pins [chip_label=CD4094]
  U1 = MAX7219 [package=dil24]  # not connected
  J1 = male pin header, 12 pins [form="♂ (male)"]
  D6 = Rectifier Diode [part_number=1N4148 package="300 mil [THT]"]
  D7 = Rectifier Diode [part_number=1N4148 package="300 mil [THT]"]
  R8_2 = Resistor [tolerance=±5% resistance=680 package=THT]
  R7_2 = Resistor [tolerance=±5% resistance=680 package=THT]
  DI13 = 7 Segment Display
  D8 = Rectifier Diode [part_number=1N4148 package="300 mil [THT]"]
  D9 = Rectifier Diode [part_number=1N4148 package="300 mil [THT]"]
  D10 = Rectifier Diode [part_number=1N4148 package="300 mil [THT]"]
  D11 = Rectifier Diode [part_number=1N4148 package="300 mil [THT]"]
  D12 = Rectifier Diode [part_number=1N4148 package="300 mil [THT]"]
  D13 = Rectifier Diode [part_number=1N4148 package="300 mil [THT]"]
  J2 = male pin header, 8 pins [form="♂ (male)"]
  J3 = male pin header, 4 pins [form="♂ (male)"]
  IC6 = IC, DIP package, 16 pins [chip_label=MIC5891]
  IC7 = IC, DIP package, 20 pins [chip_label=TPIC6B595]
  IC8 = IC, DIP package, 28 pins [chip_label=HT16K33]  # not connected
  Part2 = Arduino Nano (Rev3.0)  # not connected
  IC9 = IC, DIP package, 16 pins [chip_label=MIC5891]  # not connected
  IC10 = IC, DIP package, 20 pins [chip_label=TPIC6B595]  # not connected

nets:
  GND: Arduino.GND, 8-Channel_Source.GND, Shift_Register.GND, Shift_Register.OE, C1.1, 8-Channel_Sink.0V, Shift_Register_2.GND, Shift_Register_2.OE, C2.1
  N1: Arduino.D8, Shift_Register.ST_CP, Shift_Register_2.ST_CP
  N2: Arduino.D11/MOSI, Shift_Register.DS
  N3: Arduino.D12/MISO, Shift_Register.SH_CP, Shift_Register_2.SH_CP
  VCC: Arduino.5V, Shift_Register.MR, Shift_Register.VCC, C1.0, Shift_Register_2.MR, Shift_Register_2.VCC, C2.0
  N4: 8-Channel_Source.In_1, Shift_Register.Q0
  N5: 8-Channel_Source.In_2, Shift_Register.Q1
  N6: 8-Channel_Source.In_3, Shift_Register.Q2
  N7: 8-Channel_Source.In_4, Shift_Register.Q3
  N8: 8-Channel_Source.In_5, Shift_Register.Q4
  N9: 8-Channel_Source.In_6, Shift_Register.Q5
  N10: 8-Channel_Source.In_7, Shift_Register.Q6
  N11: 8-Channel_Source.In_8, Shift_Register.Q7
  12V: 8-Channel_Source.Vcc
  N12: 8-Channel_Source.Out_8, R8.Pin_0
  N13: 8-Channel_Source.Out_7, R7.Pin_0
  N14: 8-Channel_Source.Out_6, R6.Pin_0
  N15: 8-Channel_Source.Out_5, R5.Pin_0
  N16: 8-Channel_Source.Out_4, R4.Pin_0
  N17: 8-Channel_Source.Out_3, R3.Pin_0
  N18: 8-Channel_Source.Out_2, R1.Pin_0
  N19: 8-Channel_Source.Out_1, R9.Pin_0
  N20: Shift_Register.Q7', Shift_Register_2.DS
  N21: R1.Pin_1, DI2.Segment_B, DI3.Segment_B, DI4.Segment_B, DI5.Segment_B, DI6.Segment_B
  N22: R3.Pin_1, DI2.Segment_C, DI3.Segment_C, DI4.Segment_C, DI5.Segment_C, DI6.Segment_C
  N23: R4.Pin_1, DI2.Segment_D, DI3.Segment_D, DI4.Segment_D, DI5.Segment_D, DI6.Segment_D
  N24: R5.Pin_1, DI2.Segment_E, DI3.Segment_E, DI4.Segment_E, DI5.Segment_E, DI6.Segment_E
  N25: R6.Pin_1, DI2.Segment_F, DI3.Segment_F, DI4.Segment_F, DI5.Segment_F, DI6.Segment_F
  N26: R7.Pin_1, DI2.Segment_G, DI3.Segment_G, DI4.Segment_G, DI5.Segment_G, DI6.Segment_G
  N27: R8.Pin_1, DI2.Segment_DP, DI3.Segment_DP, DI4.Segment_DP, DI5.Segment_DP, DI6.Segment_DP
  N28: DI2.common_cathode, 8-Channel_Sink.Out_4
  N29: DI2.Segment_A, DI3.Segment_A, DI4.Segment_A, DI5.Segment_A, DI6.Segment_A, R9.Pin_1
  N30: 8-Channel_Sink.In_1, Shift_Register_2.Q0
  N31: 8-Channel_Sink.In_2, Shift_Register_2.Q1
  N32: 8-Channel_Sink.In_3, Shift_Register_2.Q2
  N33: 8-Channel_Sink.In_4, Shift_Register_2.Q3
  N34: 8-Channel_Sink.In_5, Shift_Register_2.Q4
  N35: 8-Channel_Sink.In_6, Shift_Register_2.Q5
  N36: 8-Channel_Sink.In_7, Shift_Register_2.Q6
  N37: 8-Channel_Sink.In_8, Shift_Register_2.Q7
  N38: 8-Channel_Sink.Out_8, DI6.common_cathode
  N39: 8-Channel_Sink.Out_7, DI5.common_cathode
  N40: 8-Channel_Sink.Out_6, DI4.common_cathode
  N41: 8-Channel_Sink.Out_5, DI3.common_cathode
  N42: C3.0, Arduino1.5V, C4.0, IC4.pin15, IC5.pin2, IC5.pin8
  N43: C3.1, Arduino1.GND, C4.1, IC4.pin1, IC5.pin9, IC5.pin10, IC5.pin11, IC5.pin19
  N44: Arduino1.D8, IC4.pin4, IC5.pin12
  N45: Arduino1.D11/MOSI, IC4.pin3
  N46: Arduino1.D13/SCK, IC4.pin2, IC5.pin13
  N47: IC4.pin5, DI11.common_anode
  N48: IC4.pin6, DI10.common_anode
  N49: IC4.pin7, DI9.common_anode
  N50: IC4.pin8, DI8.common_anode
  N51: IC4.pin16, IC5.pin3
  N52: R14.Pin_0, IC5.pin7
  N53: R14.Pin_1, DI11.Segment_D, DI10.Segment_D, DI9.Segment_D, DI8.Segment_D
  N54: R10.Pin_0, IC5.pin17
  N55: R10.Pin_1, DI11.Segment_DP, DI10.Segment_DP, DI9.Segment_DP, DI8.Segment_DP
  N56: R15.Pin_0, IC5.pin4
  N57: R15.Pin_1, DI11.Segment_A, DI10.Segment_A, DI9.Segment_A, DI8.Segment_A
  N58: R12.Pin_0, IC5.pin15
  N59: R12.Pin_1, DI11.Segment_F, DI10.Segment_F, DI9.Segment_F, DI8.Segment_F
  N60: R11.Pin_0, IC5.pin16
  N61: R11.Pin_1, DI11.Segment_G, DI10.Segment_G, DI9.Segment_G, DI8.Segment_G
  N62: R17.Pin_0, IC5.pin6
  N63: R17.Pin_1, DI11.Segment_C, DI10.Segment_C, DI9.Segment_C, DI8.Segment_C
  N64: R13.Pin_0, IC5.pin14
  N65: R13.Pin_1, DI11.Segment_E, DI10.Segment_E, DI9.Segment_E, DI8.Segment_E
  N66: R16.Pin_0, IC5.pin5
  N67: R16.Pin_1, DI11.Segment_B, DI10.Segment_B, DI9.Segment_B, DI8.Segment_B
  N68: DI12.Segment_A, R18.Pin_0
  N69: DI12.Segment_F, R23.Pin_1
  N70: DI12.Segment_E, R22.Pin_1
  N71: DI12.Segment_DP, R25.Pin_1
  N72: DI12.Segment_D, R21.Pin_0
  N73: DI12.common_cathode, R20.Pin_0
  N74: DI12.Segment_G, R24.Pin_1
  N75: DI12.Segment_B, R19.Pin_0
  N76: R18.Pin_1, IC1.pin4
  N77: R19.Pin_1, IC1.pin5
  N78: R20.Pin_1, IC1.pin6
  N79: R21.Pin_1, IC1.pin7
  N80: R22.Pin_0, IC1.pin14
  N81: R23.Pin_0, IC1.pin13
  N82: R24.Pin_0, IC1.pin12
  N83: R25.Pin_0, IC1.pin11
  N84: Part1.GND, IC1.pin8
  N85: Part1.D10, IC1.pin1
  N86: Part1.D11/MOSI, IC1.pin2
  N87: Part1.5V, IC1.pin15, IC1.pin16
  N88: Part1.D13/SCK, IC1.pin3
  N89: J1.pin1, R8_2.Pin_1, J2.pin8, IC7.pin17, IC7.pin18
  N90: J1.pin2, R7_2.Pin_1, J2.pin7, IC7.pin16
  N91: J1.pin3, J2.pin6, IC7.pin15
  N92: J1.pin4, J2.pin1, IC7.pin3, IC7.pin4
  N93: J1.pin5, J2.pin4, IC7.pin7, IC7.pin12, IC7.pin13
  N94: J1.pin6, J2.pin3, IC7.pin6
  N95: J1.pin7, J2.pin2, IC7.pin5
  N96: J1.pin8, J2.pin5, IC7.pin14
  N97: J1.pin9, J3.pin4, IC6.pin8
  N98: J1.pin10, J3.pin3, IC6.pin7
  N99: J1.pin11, J3.pin2, IC6.pin6
  N100: J1.pin12, DI13.Segment_E, J3.pin1, IC6.pin5
  N101: D6.cathode, R7_2.Pin_0, D9.cathode
  N102: D6.anode, DI13.Segment_F
  N103: D7.cathode, R8_2.Pin_0
  N104: D7.anode, DI13.Segment_G
  N105: DI13.Segment_D, D10.anode
  N106: DI13.common_anode, D9.anode, D12.anode
  N107: DI13.Segment_C, D13.anode
  N108: DI13.Segment_B, D11.anode
  N109: DI13.Segment_A, D8.anode

notes:
  1.8" FEM-1801L0BGW Common Cathode 7-Segment LEDs
  (http://www.farnell.com/datasheets/99300.pdf)
  Vf = 5.55V, IF = 25 mA
  Pin 8, Green = Latch
  Pin 11, Blue = Data
  Pin 12, Yellow = Clock
  With 12V source, current-limiting resistor required for LED is:
  (12 - 5.5) / 0.025 = 260Ω
  Be conservative with 330Ω on each anode.
  DP has less LEDs so requires greater resistor = 470Ω7
  Note that resistors need to be added *per segment*, not per digit. So, the wiring below is shown for a common cathode LED.
  If using a common anode LED, then the resistors should be added before the ULN2803 instead.
  12V DC
  COMMON ANODE display
  https://www.ti.com/lit/ds/symlink/cd4094b.pdf
  This is the arrangement used in the top 3x3 7 segment displays at the top of the "Magic 100" machine.
  FN1-1002R3400 GW FORGE F
  Common Anode, Vf 3.8V, If 20mA
  Use of 4.7k resistors but assuming a 12V power source:
  (12 - 3.8) / 0.02 = 410?
  Rather than multiplexing several digit displays using a combination of high-side/low-side drivers, another possibility is to use a (power) shift register *per digit*
  MAX7219 is designed only for Common Cathode displays (because, although there's 8 segment and 8 digit drivers, they're not equivalent - it has low current cathode column driver, and high current anode digit driver)
  This is the arrangement used in the top 4-digit 7-segment display at the top of the "Max-A-Million" machine.
  OasisTek TOS-15102BE-1
  Explanation at https://www.oasistek.com/pdf/led%20display.pdf
  Orange, Common Anode, Vf2.0V, If 20mA
  So, at 12V, that would suggest (12-2)/0.02 = 500Ω resistor should be placed on each segment.
  But, since displays were being multiplexed, average voltage was actually
  The board on which the 4 displays were mounted also had 32x 1N4148 diodes and 8x 680Ω resistors, which sounded promising that appropriate current-limiting was already in place, and the edge connector pins could be connected directly to 12V.
  The way they were arranged suggested that there were 8 diodes and 2 resistors corresponding to each digit, but it was actually more complicated than that (and the numbering system assigned to the diodes was completely baffling), so required some work with the multimeter to figure out what was going on - I'm assuming that this was a hacky way of trying to keep constant brightness.
  The common anode of each digit was connected directly to one of the edge connector pins.
  The individual segment cathodes were each connected to their own 1N4148 diode, and then routed to one of the eight resistors on the board (*not*, as I first assumed, to one of the two resistors on the section of board behind that digit). But the mapping of segments to diodes, and diodes to resistors, seemed very strange and took some time to map out:
  HT16K33, like the MAX7219, is designed only for Common Cathode displays. It varies from the MAX7219 in that:
  - it can control 16x8 LEDs (twice that of the MAX7219)
  - it uses I2C interface (compared to MAX7219 SPI interface)
  Multiplexed displays, by definition, need to be continually refreshed every single frame - since the LED segments do not persist (that's literally how multiplexing works....)
  Therefore, it makes sense to offload responsibility for updating the display onto a separate chip - otherwise your main() loop risks being held up with delay() calls etc., which could affect input responsiveness.
  While the two solutions above CAN be bastardised to multiplex Common Anode display (see, e.g.
  https://marco-difeo.de/2013/02/21/drive-max7219max7221-with-common-anode-displays/
  https://www.plingboot.com/2017/01/max7219-and-common-anode-displays/ )
  It requires additional hardware, and software modification.
  So, an alternative is to use a MCU with high/low-side drivers that can be customised to control pretty much any configuration of LED
  Multiplexed Common Cathode
  Multiplexed Common Anode
  Non-Multiplexed Common Anode

custom parts:
  DIP - 18 pins: Recommended for high-side switching applications that benefit from separate logic and load grounds, these devices encompass load supply voltages to 50 V and output currents to -500 mA. These 8-channel source drivers are useful for interfacing between low-level logic and high-current loads. Typical loads include relays, solenoids, lamps, stepper and/or servo motors, print hammers, and LEDs.
