# Fritzing sketch FruitMachineLamps (saved by Fritzing 0.9.3b)
breadboards: 2

parts:
  IC1 = IC, DIP package, 16 pins [chip_label=MIC5891]
  Part1 = Arduino Nano (Rev3.0)
  JACK1 = 2.1mm Barrel Jack with Terminal Block
  LED4 = LEDs [package=led10mm]
  LED3 = LEDs [package=led10mm]
  LED5 = LEDs [package=led10mm]
  LED1 = LEDs [package=led10mm]
  LED6 = LEDs [package=led10mm]
  LED8 = LEDs [package=led10mm]
  LED7 = LEDs [package=led10mm]
  LED2 = LEDs [package=led10mm]
  Part2 = Arduino Nano (Rev3.0)
  JACK2 = 2.1mm Barrel Jack with Terminal Block
  LED9 = LEDs [package=led10mm]
  LED10 = LEDs [package=led10mm]
  LED11 = LEDs [package=led10mm]
  LED12 = LEDs [package=led10mm]
  LED13 = LEDs [package=led10mm]
  LED14 = LEDs [package=led10mm]
  LED15 = LEDs [package=led10mm]
  LED16 = LEDs [package=led10mm]
  IC2 = IC, DIP package, 20 pins [chip_label=TPIC6B595]
  C1 = Ceramic Capacitor [capacitance=100nF package="100 mil [THT, multilayer]"]
  LED17 = LEDs [package=led10mm]
  LED18 = LEDs [package=led10mm]
  LED19 = LEDs [package=led10mm]
  LED20 = LEDs [package=led10mm]
  LED21 = LEDs [package=led10mm]
  LED22 = LEDs [package=led10mm]
  LED23 = LEDs [package=led10mm]
  LED24 = LEDs [package=led10mm]
  LED25 = LEDs [package=led10mm]
  LED26 = LEDs [package=led10mm]
  LED27 = LEDs [package=led10mm]
  LED28 = LEDs [package=led10mm]
  LED29 = LEDs [package=led10mm]
  LED30 = LEDs [package=led10mm]
  LED31 = LEDs [package=led10mm]
  LED32 = LEDs [package=led10mm]
  8-Channel_Source2 = DIP - 18 pins [package="DIP (Dual Inline) [THT]"]
  Shift_Register2 = 74HC595 [package="DIP16 [THT]"]

nets:
  N1: IC1.pin1, Part1.GND, JACK1.NEG, LED4.C, LED3.C, LED5.C, LED1.C, LED6.C, LED8.C, LED7.C, LED2.C, LED21.A, LED22.A, LED23.A, LED23.C, LED24.A, LED25.A, LED26.A, LED27.A, LED28.A
  N2: IC1.pin2, Part1.D13/SCK
  N3: IC1.pin3, Part1.D11/MOSI
  N4: IC1.pin4, Part1.D10
  N5: IC1.pin5, LED5.A, LED25.C
  N6: IC1.pin6, LED6.A, LED26.C
  N7: IC1.pin7, LED7.A, LED27.C
  N8: IC1.pin8, LED8.A, LED28.C
  N9: IC1.pin9, LED4.A, LED24.C
  N10: IC1.pin10, LED3.A
  N11: IC1.pin11, LED2.A, LED22.C
  N12: IC1.pin12, LED1.A, LED21.C
  N13: IC1.pin13, JACK1.POS
  N14: IC1.pin14, Part1.D5
  N15: IC1.pin15, Part1.5V
  N16: Part2.GND, JACK2.NEG, IC2.pin9, IC2.pin10, IC2.pin11, IC2.pin19, C1.1
  N17: Part2.D10, IC2.pin12
  N18: Part2.D11/MOSI, IC2.pin3
  N19: Part2.5V, IC2.pin2, IC2.pin8, C1.0
  N20: Part2.D13/SCK, IC2.pin13
  N21: JACK2.POS, LED9.A, LED10.A, LED11.A, LED12.A, LED13.A, LED14.A, LED15.A, LED16.A, LED17.C, LED18.C, LED19.C, LED20.C, LED29.C, LED30.C, LED31.C, LED32.C
  N22: LED9.C, IC2.pin17, LED17.A
  N23: LED10.C, IC2.pin16, LED18.A
  N24: LED11.C, IC2.pin15, LED19.A
  N25: LED12.C, IC2.pin14, LED20.A
  N26: LED13.C, IC2.pin7, LED32.A
  N27: LED14.C, IC2.pin6, LED31.A
  N28: LED15.C, IC2.pin5, LED30.A
  N29: LED16.C, IC2.pin4, LED29.A
  N30: 8-Channel_Source2.In_1, Shift_Register2.Q7
  N31: 8-Channel_Source2.In_2, Shift_Register2.Q6
  N32: 8-Channel_Source2.In_3, Shift_Register2.Q5
  N33: 8-Channel_Source2.In_4, Shift_Register2.Q4
  N34: 8-Channel_Source2.In_5, Shift_Register2.Q3
  N35: 8-Channel_Source2.In_6, Shift_Register2.Q2
  N36: 8-Channel_Source2.In_7, Shift_Register2.Q1
  N37: 8-Channel_Source2.In_8, Shift_Register2.Q0, Shift_Register2.VCC

notes:
  The MIC5891 is a high-side 8-channel shift register. It provides equivalent functionality to a 74HC595 and UDN2981 - allowing an Arduino to control a current source <50V@500mA to up to 8 devices via a single serial data in pin. More devices can be daisy-chained together if required. If the OE pin is connected to a PWM-capable pin, the output voltage can be adjusted.
  Arduino MIC5891
  GND GND (Pin 1)
  5V Logic Supply (Pin 15)
  13 Clock (Pin 2)
  11 Serial Data In (Pin 3)
  10 Strobe (Pin 4)
  5 (PWM) Output Enable (Pin 14)
  ---
  12V Load Supply (Pin 13)
  ---
  Lamp +ve Outputs 1-8 (Pins 5-12)
  Pin 16, unused in this example, is the serial data out which can be connected to the serial data in of another MIC5891.
  12V
  The MIC5891 directs this supply to the 8 output channels according to the data data received from the Arduino on the serial in pin
  SERCK = Clock (normally D13, but can be any pin)
  RCK = Strobe/Latch/SS (normally D10, but can be any pin)
  SERIN = Data/MOSI (normally D11, but can be any)
  G¬ should be pulled LOW (to GND)
  SRCLR should be pulled HIGH (to 5V)
  All GNDs to GND
  VCC to 5V
  The TPIC6B595 sinks current from the 8 output channels according to the data data received from the Arduino on the serial in pin
  Low-side switch with TPIC6B595
  High-side switch with MIC5891

custom parts:
  LEDs: LEDs Standard schematic elements and footprints for 5mm, 3mm, 1206, and 0603 sized LEDs. 5mm - Spark Fun Electronics SKU : COM-00529 (and others)
  DIP - 18 pins: Recommended for high-side switching applications that benefit from separate logic and load grounds, these devices encompass load supply voltages to 50 V and output currents to -500 mA. These 8-channel source drivers are useful for interfacing between low-level logic and high-current loads. Typical loads include relays, solenoids, lamps, stepper and/or servo motors, print hammers, and LEDs.
