# Fritzing sketch FruitMachineOptoSensors (saved by Fritzing 0.9.3b)

parts:
  IC1 = IC, DIP package, 14 pins [chip_label=TC4093BP]
  LED1 = LED - 5mm [color="Red (633nm)" package="5 mm [THT]"]
  Q1 = PNP-Transistor [package="TO92 [THT]"]
  Mod5 = KY-010 Photo Interrupter Module [package="Breakout board"]  # not connected
  Part1 = Arduino Nano (Rev3.0)
  R6 = Resistor [tolerance=±5% resistance=220 package=THT]
  J1 = male pin header, 2 pins [form="♂ (male)"]
  J2 = male pin header, 2 pins [form="♂ (male)"]
  R7 = Resistor [tolerance=±5% resistance=10k package=THT]
  R3 = Resistor [tolerance=±5% resistance=56k package=THT]
  R2 = Resistor [tolerance=±1% resistance=470 package=THT]
  R1 = Resistor [tolerance=±5% resistance=10k package=THT]
  J3 = male pin header, 5 pins [form="♂ (male)"]
  J4 = female pin header, 2 pins [form="♀ (female)"]
  J5 = female pin header, 1 pin [form="♀ (female)"]

nets:
  N1: IC1.pin3, R1.Pin_0
  N2: IC1.pin5, IC1.pin12
  N3: IC1.pin6, IC1.pin9
  N4: IC1.pin7, Q1.E, R3.Pin_0, J3.pin5
  N5: IC1.pin14, R2.Pin_1, J3.pin3, J5.pin1
  N6: LED1.anode, R2.Pin_0
  N7: Q1.B, R1.Pin_1
  N8: Q1.C, J3.pin4
  N9: Part1.GND, J1.pin1, J2.pin2
  N10: Part1.D2, J1.pin2, R7.Pin_1
  N11: Part1.5V, R6.Pin_0, R7.Pin_0
  N12: R6.Pin_1, J2.pin1
  N13: J3.pin1, J4.pin1
  N14: J3.pin2, J4.pin2

notes:
  Some models use OMRON 4235 "transmissive photomicrosensor" https://omronfs.omron.com/en_US/ecb/products/pdf/en-ee_sx4235a_p2.pdf
  This only has three wires:
  VCC (5V)
  Signal Out
  GND
  (the base of the board shows the internal wiring, which looks very similar to the Sparkfun Photo Interruptor breakout board, except with a 390Ω resistor in place of a 220Ω resistor)
  OMRON 4235
  "Homemade"
  See https://www.utopiamechanicus.com/article/opto-interrupter-part-3/
  http://www.martyncurrey.com/connecting-an-photo-interrupter-to-an-arduino/
  https://5.imimg.com/data5/YL/TX/MY-1833510/photoelectric-switch-hy860d.pdf
  Circuit below works with sensor pin set to INPUT, in which case reads 0 when the sensor is unobstructed, or 1 when there is an object in the way.
  Starpoint A1645 iss.3
  Uses "B520" opto switch, with additional IC (TC4093BP), transistor (ZTX450), LED and a bunch of resistors. The wiring is an absoulute hot mess and I ended up blowing this up, so don't really know how it's meant to be wired!
  B520
  A
  220Ω
  10kΩ
  HY-860D

custom parts:
  KY-010 Photo Interrupter Module: KY-010 Photo Interrupter Module, it will trigger a signal when light between the sensor's gap is blocked.
