# Fritzing sketch FruitMachineReels (saved by Fritzing 0.9.3b)

parts:
  Mod5 = KY-010 Photo Interrupter Module [package="Breakout board"]
  M1 = Stepper Motor - Unipolar
  LED1 = LED - 5mm [color="White (4500K)" package="5 mm [THT]"]
  LED2 = LED - 5mm [color="White (4500K)" package="5 mm [THT]"]
  LED3 = LED - 5mm [color="White (4500K)" package="5 mm [THT]"]
  J1 = female pin header, 15 pins [form="♀ (female)"]
  R1 = Resistor [tolerance=±5% resistance=220 package=THT]
  J2 = female pin header, 15 pins [form="♀ (female)"]  # not connected
  J3 = female pin header, 15 pins [form="♀ (female)"]
  J4 = female pin header, 13 pins [form="♀ (female)"]
  J6 = female pin header, 15 pins [form="♀ (female)"]
  J7 = female pin header, 15 pins [form="♀ (female)"]  # not connected
  J5 = female pin header, 15 pins [form="♀ (female)"]

nets:
  N1: Mod5.-, J1.pin11
  N2: Mod5.Vin, R1.Pin_0
  N3: Mod5.S, J1.pin10
  N4: M1.A, J1.pin3
  N5: M1.COMMON_1, J1.pin1
  N6: M1.C, J1.pin4
  N7: M1.B, J1.pin5
  N8: M1.COMMON_2, J1.pin2
  N9: M1.D, J1.pin6
  N10: LED1.cathode, LED2.cathode, LED3.cathode, J1.pin15
  N11: LED1.anode, J1.pin12
  N12: LED2.anode, J1.pin13
  N13: LED3.anode, J1.pin14
  N14: J1.pin9, R1.Pin_1
  N15: J3.pin1, J3.pin2, J4.pin1
  N16: J3.pin3, J4.pin9
  N17: J3.pin4, J4.pin8
  N18: J3.pin5, J4.pin7
  N19: J3.pin6, J4.pin6
  N20: J3.pin9, J4.pin2
  N21: J3.pin10, J4.pin3
  N22: J3.pin11, J4.pin5
  N23: J3.pin12, J4.pin13
  N24: J3.pin13, J4.pin11
  N25: J3.pin14, J4.pin12
  N26: J3.pin15, J4.pin10
  N27: J6.pin1, J5.pin1
  N28: J6.pin2, J5.pin2
  N29: J6.pin3, J5.pin3
  N30: J6.pin4, J5.pin4
  N31: J6.pin5, J5.pin5
  N32: J6.pin6, J5.pin6, J5.pin7
  N33: J6.pin8, J5.pin8
  N34: J6.pin9, J5.pin9
  N35: J6.pin10, J5.pin10
  N36: J6.pin11, J5.pin11
  N37: J6.pin12, J5.pin12
  N38: J6.pin13, J5.pin13
  N39: J6.pin14, J5.pin14
  N40: J6.pin15, J5.pin15

notes:
  1. Common A (unused) (Green)
  2. Common B (unused) (Green)
  3. A1 (Red)
  4. A2 (Yellow)
  5. B1 (Blue)
  6. B2 (Black)
  7. N/C
  8. N/C
  9. 5V Opto Vin (Pink)
  10. Signal Opto (Brown)
  11. Opto GND (Purple/Blue)
  12. Hi Lamp 12V
  13. Mid Lamp 12V
  14. Low Lamp 12V
  15. GND Lamps
  Opto Sensor out goes HIGH when obstructed.
  See:
  https://omronfs.omron.com/en_US/ecb/products/pdf/en-ee_sx4235a_p2_discon.pdf
  https://omronfs.omron.com/en_US/ecb/products/pdf/en-ph_technical.pdf
  Lamps share a common ground, and separately switched +12V
  Unipolar stepper motor (normally 12V, sometimes 24V) has 6 wires (2 sets of 3), but it is not necessary to use the common wire of each pair
  This is the harness used in "Max-A-Million"
  1. Common (unused) (Orange)
  2. 5V (Red)
  3. Opto Signal (White/Black)
  4. N/C
  5. Opto GND (Black)
  6. B2 (White/Brown)
  7. B1 (White/Red)
  8. A2 (White/Orange)
  9. A1 (White/Yellow)
  10. GND Lamps (Orange)
  11. Mid Lamp 12V (White/Green)
  12. Low Lamp 12V (White/Blue)
  13. High Lamp 12V (White/Purple)
  This is the harness used in "Snakes & Ladders"
  1. Common A (unused) (Green)
  2. Common B (unused) (Green)
  3. A1 (Black)
  4. A2 (Black)
  5. B1 (Black)
  6. B2 (Black)
  7. N/C
  8. N/C (Black)
  9. 5V Opto Vin (Yellow)
  10. Signal Opto (Black)
  11. Opto GND (Black)
  12. Hi Lamp 12V (Purple)
  13. Mid Lamp 12V(Purple)
  14. Low Lamp 12V (Purple)
  15. GND Lamps (Black)

custom parts:
  KY-010 Photo Interrupter Module: KY-010 Photo Interrupter Module, it will trigger a signal when light between the sensor's gap is blocked.
