# Fritzing sketch VFD Displays (saved by Fritzing 0.9.3b)

parts:
  J2 = male pin header, 2 pins [form="♂ (male)"]
  J1 = male pin header, 3 pins [form="♂ (male)"]
  J3 = female pin header, 1 pin [form="♀ (female)"]  # not connected
  Part1 = Arduino Nano (Rev3.0)
  JACK1 = 2.1mm Barrel Jack with Terminal Block
  J4 = female pin header, 1 pin [form="♀ (female)"]  # not connected
  Part2 = Arduino Nano (Rev3.0)
  JACK2 = 2.1mm Barrel Jack with Terminal Block
  J6 = male pin header, 4 pins [form="♂ (male)"]
  J5 = male pin header, 1 pin [form="♂ (male)"]
  J7 = male pin header, 6 pins [form="♂ (male)"]
  Part4 = Arduino Nano (Rev3.0)
  JACK3 = 2.1mm Barrel Jack with Terminal Block
  J8 = male pin header, 4 pins [form="♂ (male)"]
  J9 = male pin header, 6 pins [form="♂ (male)"]
  J10 = male pin header, 1 pin [form="♂ (male)"]
  J11 = female pin header, 1 pin [form="♀ (female)"]  # not connected
  J12 = male pin header, 6 pins [form="♂ (male)"]  # not connected

nets:
  N1: J2.pin1, Part1.D13/SCK
  N2: J2.pin2, JACK1.POS
  N3: J1.pin1, Part1.GND, JACK1.NEG
  N4: J1.pin2, Part1.D8
  N5: J1.pin3, Part1.D11/MOSI
  N6: Part2.GND, JACK2.NEG, J6.pin1, J7.pin1
  N7: Part2.D8, J7.pin2
  N8: Part2.D10, J6.pin4
  N9: Part2.D11/MOSI, J6.pin2
  N10: Part2.D13/SCK, J6.pin3, J7.pin3
  N11: JACK2.POS, J5.pin1, J7.pin6
  N12: Part4.GND, JACK3.NEG, J8.pin1, J9.pin1
  N13: Part4.D8, J9.pin2
  N14: Part4.D10, J8.pin4
  N15: Part4.D11/MOSI, J8.pin2
  N16: Part4.D13/SCK, J8.pin3, J9.pin3
  N17: JACK3.POS, J9.pin6, J10.pin1

notes:
  31-821-001 ISS 1
  (From Top)
  Pin 1 GND
  Pin 2 RST
  Pin 3 DATA
  Pin 4 N/C
  Pin 5 CLK
  Pin 6 +12V
  16L102DA4
  (As viewed from reverse, from bottom)
  Pin 1,2 VCC (12V)
  Pin 3 No Pin
  Pin 4, 6 N/C
  Pin 5 SELECT
  Pin 7,8 CLK
  Pin 9 DATA
  Pin 10 RST
  Pin 11/12 GND
  31-821-001 ISS 1 with a NEC chip from "Snakes & Ladders"
  Samsung 16L02DA4 board with a OKI M9202-04 chip from "Tuppenny Nudger"
  12V
  Samsung 16LF01UA3 starburst (16-seg) board with from "Max-A-Million". NOTE 5V!
  (As viewed from reverse, from bottom)
  Pin 1,2 VCC (5V)
  Pin 3 No Pin
  Pin 4, 6 N/C
  Pin 5 SELECT
  Pin 7,8 CLK
  Pin 9 DATA
  Pin 10 RST
  Pin 11/12 GND
  5V, 800mA
  There is a secondary, simpler set of pins, as follows:
  GND
  RST
  DATA
  SEL
  CLK
  5V
  Understanding SAMSUNG Display Parts numbers
  e.g. 16L02DA4
  16 - num of characters
  L - size (S/M/L)
  02 - number of lines
  DA - interface (DA = UART (TTL), UA = SPI)
  4 = voltage supply (4=12V, 3=5V)
  (for more examples, see https://www.giant-supplier.com/VFDDisplaySamsung.htm)
  Also works for GU96X8M displays
