# Fritzing sketch HC74595 and UDN2981 FruitMachine LED (saved by Fritzing 0.9.3b)
circuit board: 8.46667cm x 5.64444cm
breadboards: 1

parts:
  Part1 = Arduino Nano (Rev3.0)
  UDN_2981_-_8-Channel_Source_Driver1 = DIP - 18 pins [package="DIP (Dual Inline) [THT]"]
  U1 = 74HC595 [package="DIP16 [THT]"]
  C1 = Ceramic Capacitor [capacitance=100nF package="100 mil [THT, multilayer]"]
  R1 = Resistor [tolerance=±5% resistance=330 package=THT]
  R3 = Resistor [tolerance=±5% resistance=330 package=THT]
  R4 = Resistor [tolerance=±5% resistance=330 package=THT]
  R5 = Resistor [tolerance=±5% resistance=330 package=THT]
  R6 = Resistor [tolerance=±5% resistance=330 package=THT]
  R7 = Resistor [tolerance=±5% resistance=330 package=THT]
  R8 = Resistor [tolerance=±5% resistance=330 package=THT]
  DI2 = 7 Segment Display
  IC1 = ULN2803A [package=THT]
  DI3 = 7 Segment Display
  DI4 = 7 Segment Display
  DI5 = 7 Segment Display
  DI6 = 7 Segment Display
  R9 = Resistor [tolerance=±5% resistance=330 package=THT]

nets:
  GND: Part1.GND, UDN_2981_-_8-Channel_Source_Driver1.GND, U1.GND, U1.OE, C1.1, IC1.0V
  N1: Part1.D8, U1.ST_CP
  N2: Part1.D11/MOSI, U1.DS
  N3: Part1.D12/MISO, U1.SH_CP
  N4: Part1.A4, IC1.In_5
  N5: Part1.A3, IC1.In_4
  N6: Part1.A2, IC1.In_3
  N7: Part1.A1, IC1.In_2
  N8: Part1.A0, IC1.In_1
  N9: UDN_2981_-_8-Channel_Source_Driver1.In_1, U1.Q0
  N10: UDN_2981_-_8-Channel_Source_Driver1.In_2, U1.Q1
  N11: UDN_2981_-_8-Channel_Source_Driver1.In_3, U1.Q2
  N12: UDN_2981_-_8-Channel_Source_Driver1.In_4, U1.Q3
  N13: UDN_2981_-_8-Channel_Source_Driver1.In_5, U1.Q4
  N14: UDN_2981_-_8-Channel_Source_Driver1.In_6, U1.Q5
  N15: UDN_2981_-_8-Channel_Source_Driver1.In_7, U1.Q6
  N16: UDN_2981_-_8-Channel_Source_Driver1.In_8, U1.Q7
  12V: UDN_2981_-_8-Channel_Source_Driver1.Vcc
  N17: UDN_2981_-_8-Channel_Source_Driver1.Out_8, R8.Pin_0
  N18: UDN_2981_-_8-Channel_Source_Driver1.Out_7, R7.Pin_0
  N19: UDN_2981_-_8-Channel_Source_Driver1.Out_6, R6.Pin_0
  N20: UDN_2981_-_8-Channel_Source_Driver1.Out_5, R5.Pin_0
  N21: UDN_2981_-_8-Channel_Source_Driver1.Out_4, R4.Pin_0
  N22: UDN_2981_-_8-Channel_Source_Driver1.Out_3, R3.Pin_0
  N23: UDN_2981_-_8-Channel_Source_Driver1.Out_2, R1.Pin_0
  N24: UDN_2981_-_8-Channel_Source_Driver1.Out_1, R9.Pin_0
  N25: U1.MR, U1.VCC, C1.0
  N26: R1.Pin_1, DI2.Segment_B, DI3.Segment_B, DI4.Segment_B, DI5.Segment_B, DI6.Segment_B
  N27: R3.Pin_1, DI2.Segment_C, DI3.Segment_C, DI4.Segment_C, DI5.Segment_C, DI6.Segment_C
  N28: R4.Pin_1, DI2.Segment_D, DI3.Segment_D, DI4.Segment_D, DI5.Segment_D, DI6.Segment_D
  N29: R5.Pin_1, DI2.Segment_E, DI3.Segment_E, DI4.Segment_E, DI5.Segment_E, DI6.Segment_E
  N30: R6.Pin_1, DI2.Segment_F, DI3.Segment_F, DI4.Segment_F, DI5.Segment_F, DI6.Segment_F
  N31: R7.Pin_1, DI2.Segment_G, DI3.Segment_G, DI4.Segment_G, DI5.Segment_G, DI6.Segment_G
  N32: R8.Pin_1, DI2.Segment_DP, DI3.Segment_DP, DI4.Segment_DP, DI5.Segment_DP, DI6.Segment_DP
  N33: DI2.common_cathode, IC1.Out_1
  N34: DI2.Segment_A, DI3.Segment_A, DI4.Segment_A, DI5.Segment_A, DI6.Segment_A, R9.Pin_1
  N35: IC1.Out_5, DI6.common_cathode
  N36: IC1.Out_4, DI5.common_cathode
  N37: IC1.Out_3, DI4.common_cathode
  N38: IC1.Out_2, DI3.common_cathode

notes:
  1.8" FEM-1801L0BGW Common Cathode 7-Segment LEDs
  (http://www.farnell.com/datasheets/99300.pdf)
  Vf = 5.55V, IF = 25 mA
  DS, Blue = Data
  ST, Green = Latch
  SH, Yellow = Clock
  With 12V source, current-limiting resistor required for LED is:
  (12 - 5.5) / 0.025 = 260Ω
  Be on safe side with 330Ω on each anode
  12V DC

custom parts:
  DIP - 18 pins: Recommended for high-side switching applications that benefit from separate logic and load grounds, these devices encompass load supply voltages to 50 V and output currents to -500 mA. These 8-channel source drivers are useful for interfacing between low-level logic and high-current loads. Typical loads include relays, solenoids, lamps, stepper and/or servo motors, print hammers, and LEDs.
